// Logisim project C209.circ as structural Verilog: 12 circuits, main circuit meioSomador
module meioSomador (
  input  A,
  input  B,
  output S,
  output Cout
);

  xor xor_1 (S, A, B);
  and and_1 (Cout, A, B);
endmodule

module somadorCompleto (
  input  A,
  input  B,
  input  Cin,
  output S,
  output Cout
);

  wire meiosomador_1_cout, meiosomador_1_s, meiosomador_2_cout;

  meioSomador meiosomador_1 (.Cout(meiosomador_1_cout), .B(B), .S(meiosomador_1_s), .A(A));
  meioSomador meiosomador_2 (.Cout(meiosomador_2_cout), .B(Cin), .S(S), .A(meiosomador_1_s));
  or or_1 (Cout, meiosomador_2_cout, meiosomador_1_cout);
endmodule

module somador_4bits (
  input  [3:0] in_1,
  input  [3:0] in_2,
  output [3:0] out_3
);

  wire somadorcompleto_1_cout, somadorcompleto_2_cout, somadorcompleto_3_cout, somadorcompleto_4_cout;

  somadorCompleto somadorcompleto_1 (
    .Cout(somadorcompleto_1_cout), .Cin(somadorcompleto_2_cout), .S(out_3[3]), .A(in_1[3]), .B(in_2[3]));
  somadorCompleto somadorcompleto_2 (
    .Cout(somadorcompleto_2_cout), .Cin(somadorcompleto_3_cout), .S(out_3[2]), .A(in_1[2]), .B(in_2[2]));
  Hex_Digit_Display hex_digit_display_1 (.value(out_3));  // open: dp
  somadorCompleto somadorcompleto_3 (
    .Cout(somadorcompleto_3_cout), .Cin(somadorcompleto_4_cout), .S(out_3[1]), .A(in_1[1]), .B(in_2[1]));
  somadorCompleto somadorcompleto_4 (.Cout(somadorcompleto_4_cout), .Cin(1'b0), .S(out_3[0]), .A(in_1[0]), .B(in_2[0]));
  // also tied to GND on the sheet: somadorcompleto_1_cout
endmodule

module complemento2 (
  input  [3:0] A,
  input  [3:0] B,
  input  Cin,
  output Cout,
  output [3:0] S
);

  wire multiplexer_1_out, multiplexer_2_out, multiplexer_3_out, multiplexer_4_out, not_1_out, not_2_out,
       not_3_out, not_4_out, somadorcompleto_2_cout, somadorcompleto_3_cout, somadorcompleto_4_cout;

  not not_1 (not_1_out, B[3]);
  Multiplexer #(.enable("false")) multiplexer_1 (.in0(B[3]), .in1(not_1_out), .out(multiplexer_1_out), .sel(Cin));
  somadorCompleto somadorcompleto_1 (
    .Cout(Cout), .Cin(somadorcompleto_2_cout), .S(S[3]), .A(A[3]), .B(multiplexer_1_out));
  Multiplexer #(.enable("false")) multiplexer_2 (.in0(B[2]), .in1(not_2_out), .out(multiplexer_2_out), .sel(Cin));
  not not_2 (not_2_out, B[2]);
  somadorCompleto somadorcompleto_2 (
    .Cout(somadorcompleto_2_cout), .Cin(somadorcompleto_3_cout), .S(S[2]), .A(A[2]), .B(multiplexer_2_out));
  not not_3 (not_3_out, B[1]);
  Multiplexer #(.enable("false")) multiplexer_3 (.in0(B[1]), .in1(not_3_out), .out(multiplexer_3_out), .sel(Cin));
  somadorCompleto somadorcompleto_3 (
    .Cout(somadorcompleto_3_cout), .Cin(somadorcompleto_4_cout), .S(S[1]), .A(A[1]), .B(multiplexer_3_out));
  not not_4 (not_4_out, B[0]);
  Multiplexer #(.enable("false")) multiplexer_4 (.in0(B[0]), .in1(not_4_out), .out(multiplexer_4_out), .sel(Cin));
  somadorCompleto somadorcompleto_4 (
    .Cout(somadorcompleto_4_cout), .Cin(Cin), .S(S[0]), .A(A[0]), .B(multiplexer_4_out));
endmodule

module multiplicador (
  input  A1,
  input  A0,
  input  B1,
  input  B0,
  output P3,
  output P2,
  output P1,
  output P0
);

  wire and_1_out, and_2_out, and_3_out, meiosomador_2_cout;

  and and_1 (and_1_out, A1, B1);
  meioSomador meiosomador_1 (.Cout(P3), .B(and_1_out), .S(P2), .A(meiosomador_2_cout));
  and and_2 (and_2_out, A1, B0);
  and and_3 (and_3_out, A0, B1);
  meioSomador meiosomador_2 (.Cout(meiosomador_2_cout), .B(and_2_out), .S(P1), .A(and_3_out));
  and and_4 (P0, A0, B0);
endmodule

module deslocador (
  input  [7:0] A,
  input  [2:0] SA,
  output [7:0] out_3
);

  Shifter shifter_1 (.in(A), .\dist (SA), .out(out_3));
endmodule

module registradorDesloc_CP (
  input  [3:0] D,
  input  Clock,
  input  Carga,
  input  Clear,
  output [3:0] Q
);

  wire multiplexer_1_out, multiplexer_2_out, multiplexer_3_out, multiplexer_4_out;

  Multiplexer #(.enable("false")) multiplexer_1 (.in0(Q[3]), .in1(D[3]), .out(multiplexer_1_out), .sel(Carga));
  D_Flip_Flop d_ff_1 (.D(multiplexer_1_out), .clk(Clock), .Q(Q[3]), .reset(Clear));  // open: Qn, preset
  Multiplexer #(.enable("false")) multiplexer_2 (.in0(Q[2]), .in1(D[2]), .out(multiplexer_2_out), .sel(Carga));
  D_Flip_Flop d_ff_2 (.D(multiplexer_2_out), .clk(Clock), .Q(Q[2]), .reset(Clear));  // open: Qn, preset
  Multiplexer #(.enable("false")) multiplexer_3 (.in0(Q[1]), .in1(D[1]), .out(multiplexer_3_out), .sel(Carga));
  D_Flip_Flop d_ff_3 (.D(multiplexer_3_out), .clk(Clock), .Q(Q[1]), .reset(Clear));  // open: Qn, preset
  D_Flip_Flop d_ff_4 (.D(multiplexer_4_out), .clk(Clock), .Q(Q[0]), .reset(Clear));  // open: Qn, preset
  Multiplexer #(.enable("false")) multiplexer_4 (.in0(Q[0]), .in1(D[0]), .out(multiplexer_4_out), .sel(Carga));
endmodule

module ALU (
  input  [7:0] B,
  input  [7:0] A,
  input  [3:0] OP,
  output [7:0] S
);

  wire [7:0] and_1_out, multiplier_1_out, nand_1_out, not_1_out, or_1_out, shifter_1_out, shifter_2_out,
       somador_8bits_1_out_3, subtrator_8bits_1_out_3, xnor_1_out, xor_1_out;

  Multiplier multiplier_1 (.a(A), .b(B), .out(multiplier_1_out));  // open: cin, cout
  Shifter #(.shift("lr")) shifter_1 (.in(A), .\dist (3'b010), .out(shifter_1_out));
  assign not_1_out = ~A;  // NOT_Gate not_1, 8 bits wide
  Shifter shifter_2 (.in(A), .\dist (3'b100), .out(shifter_2_out));
  subtrator_8bits subtrator_8bits_1 (.in_2(B), .in_1(A), .out_3(subtrator_8bits_1_out_3));
  assign nand_1_out = ~(A & B);  // NAND_Gate nand_1, 8 bits wide
  somador_8bits somador_8bits_1 (.in_2(B), .in_1(A), .out_3(somador_8bits_1_out_3));
  assign or_1_out = A | B;  // OR_Gate or_1, 8 bits wide
  assign xor_1_out = A ^ B;  // XOR_Gate xor_1, 8 bits wide
  assign and_1_out = A & B;  // AND_Gate and_1, 8 bits wide
  assign xnor_1_out = ~(A ^ B);  // XNOR_Gate xnor_1, 8 bits wide
  Multiplexer #(.select(4), .width(8), .enable("false")) multiplexer_1 (
    .in0({8{1'b0}}), .in1(subtrator_8bits_1_out_3), .in2(multiplier_1_out), .in3({8{1'b0}}),
    .in4(shifter_1_out), .in5(nand_1_out), .in6({8{1'b0}}), .in7(somador_8bits_1_out_3), .in8(not_1_out),
    .in9(or_1_out), .in10(xnor_1_out), .in11(shifter_2_out), .in12(xor_1_out), .in13({8{1'b0}}),
    .in14(and_1_out), .in15({8{1'b0}}), .out(S), .sel(OP));
  // Mips_ALU mips_alu_1: pin names not known

  // Notes on the sheet:
  //   SA
  //   SA
endmodule

module somador_8bits (
  input  [7:0] in_1,
  input  [7:0] in_2,
  output [7:0] out_3
);

  wire somadorcompleto_1_cout, somadorcompleto_2_cout, somadorcompleto_3_cout, somadorcompleto_4_cout,
       somadorcompleto_5_cout, somadorcompleto_6_cout, somadorcompleto_7_cout, somadorcompleto_8_cout;

  somadorCompleto somadorcompleto_1 (
    .Cout(somadorcompleto_1_cout), .Cin(somadorcompleto_2_cout), .S(out_3[7]), .A(in_1[7]), .B(in_2[7]));
  somadorCompleto somadorcompleto_2 (
    .Cout(somadorcompleto_2_cout), .Cin(somadorcompleto_3_cout), .S(out_3[6]), .A(in_1[6]), .B(in_2[6]));
  somadorCompleto somadorcompleto_3 (
    .Cout(somadorcompleto_3_cout), .Cin(somadorcompleto_4_cout), .S(out_3[5]), .A(in_1[5]), .B(in_2[5]));
  somadorCompleto somadorcompleto_4 (
    .Cout(somadorcompleto_4_cout), .Cin(somadorcompleto_5_cout), .S(out_3[4]), .A(in_1[4]), .B(in_2[4]));
  somadorCompleto somadorcompleto_5 (
    .Cout(somadorcompleto_5_cout), .Cin(somadorcompleto_6_cout), .S(out_3[3]), .A(in_1[3]), .B(in_2[3]));
  somadorCompleto somadorcompleto_6 (
    .Cout(somadorcompleto_6_cout), .Cin(somadorcompleto_7_cout), .S(out_3[2]), .A(in_1[2]), .B(in_2[2]));
  somadorCompleto somadorcompleto_7 (
    .Cout(somadorcompleto_7_cout), .Cin(somadorcompleto_8_cout), .S(out_3[1]), .A(in_1[1]), .B(in_2[1]));
  somadorCompleto somadorcompleto_8 (.Cout(somadorcompleto_8_cout), .Cin(1'b0), .S(out_3[0]), .A(in_1[0]), .B(in_2[0]));
  // also tied to GND on the sheet: somadorcompleto_1_cout
endmodule

module meioSubtrator (
  input  in_1,
  input  in_2,
  output out_3,
  output out_4
);

  wire not_1_out;

  xor xor_1 (out_3, in_1, in_2);
  not not_1 (not_1_out, in_2);
  and and_1 (out_4, in_1, not_1_out);
endmodule

module subtrator (
  input  in_1,
  input  in_2,
  input  in_3,
  output out_4,
  output out_5
);

  wire meiosubtrator_1_out_3, meiosubtrator_1_out_4, meiosubtrator_2_out_4;

  meioSubtrator meiosubtrator_1 (
    .out_4(meiosubtrator_1_out_4), .in_2(in_2), .in_1(in_1), .out_3(meiosubtrator_1_out_3));
  meioSubtrator meiosubtrator_2 (
    .out_4(meiosubtrator_2_out_4), .in_2(in_3), .in_1(meiosubtrator_1_out_3), .out_3(out_4));
  or or_1 (out_5, meiosubtrator_2_out_4, meiosubtrator_1_out_4);
endmodule

module subtrator_8bits (
  input  [7:0] in_1,
  input  [7:0] in_2,
  output [7:0] out_3
);

  wire subtrator_1_out_5, subtrator_2_out_5, subtrator_3_out_5, subtrator_4_out_5, subtrator_5_out_5,
       subtrator_6_out_5, subtrator_7_out_5, subtrator_8_out_5;

  subtrator subtrator_1 (
    .out_4(out_3[7]), .in_2(in_2[7]), .in_1(in_1[7]), .in_3(subtrator_2_out_5), .out_5(subtrator_1_out_5));
  subtrator subtrator_2 (
    .out_4(out_3[6]), .in_2(in_2[6]), .in_1(in_1[6]), .in_3(subtrator_3_out_5), .out_5(subtrator_2_out_5));
  subtrator subtrator_3 (
    .out_4(out_3[5]), .in_2(in_2[5]), .in_1(in_1[5]), .in_3(subtrator_4_out_5), .out_5(subtrator_3_out_5));
  subtrator subtrator_4 (
    .out_4(out_3[4]), .in_2(in_2[4]), .in_1(in_1[4]), .in_3(subtrator_5_out_5), .out_5(subtrator_4_out_5));
  subtrator subtrator_5 (
    .out_4(out_3[3]), .in_2(in_2[3]), .in_1(in_1[3]), .in_3(subtrator_6_out_5), .out_5(subtrator_5_out_5));
  subtrator subtrator_6 (
    .out_4(out_3[2]), .in_2(in_2[2]), .in_1(in_1[2]), .in_3(subtrator_7_out_5), .out_5(subtrator_6_out_5));
  subtrator subtrator_7 (
    .out_4(out_3[1]), .in_2(in_2[1]), .in_1(in_1[1]), .in_3(subtrator_8_out_5), .out_5(subtrator_7_out_5));
  subtrator subtrator_8 (.out_4(out_3[0]), .in_2(in_2[0]), .in_1(in_1[0]), .in_3(1'b0), .out_5(subtrator_8_out_5));
  // also tied to GND on the sheet: subtrator_1_out_5
endmodule
