// Logisim project Projeto2_A.circ as structural Verilog: 1 circuit, main circuit main
module main (
);

  wire ALU_SRC, and_2_out, and_3_out, and_4_out, and_5_out, CLOCK, LOAD, MEM_TO_REG, REG_DEST, REG_W,
       registerfile_1_p7, STORE;
  wire [3:1] ALU_OP;
  wire [4:0] mipsprogramrom_1_p2_2, multiplexer_1_out;
  wire [5:0] FUNCT;
  wire [31:0] adder_1_out, bit_extender_1_out, mips_alu_1_p4, mips_ram_1_p5, multiplexer_2_out, register_1_q,
       registerfile_1_p1, registerfile_1_p8;
  wire [31:6] mipsprogramrom_1_p2;

  Adder #(.width(32)) adder_1 (.a(register_1_q), .b(32'h4), .out(adder_1_out));  // open: cin, cout
  Register #(.width(32)) register_1 (.D(adder_1_out), .Q(register_1_q), .clk(CLOCK));  // open: en, clr
  Clock clock_1 (.out(CLOCK));
  // MIPSProgramROM mipsprogramrom_1: pin names not known; wires that end beside it: register_1_q, {mipsprogramrom_1_p2[31:26], mipsprogramrom_1_p2_2, mipsprogramrom_1_p2[20:6], FUNCT}
  and and_1 (ALU_OP[3], FUNCT[0], FUNCT[1], FUNCT[2], ~FUNCT[3], ~FUNCT[4], FUNCT[5]);  // AND_Gate
  and and_2 (and_2_out, FUNCT[0], ~FUNCT[1], ~FUNCT[2], ~FUNCT[3], ~FUNCT[4], FUNCT[5]);  // AND_Gate
  Multiplexer #(.width(5)) multiplexer_1 (
    .in0(mipsprogramrom_1_p2[15:11]), .in1(mipsprogramrom_1_p2[20:16]), .out(multiplexer_1_out),
    .sel(REG_DEST));  // open: en
  and and_3 (and_3_out, mipsprogramrom_1_p2[26], ~mipsprogramrom_1_p2[27], ~mipsprogramrom_1_p2[28], mipsprogramrom_1_p2[29], ~mipsprogramrom_1_p2[30], ~mipsprogramrom_1_p2[31]);  // AND_Gate
  and and_4 (and_4_out, mipsprogramrom_1_p2[26], mipsprogramrom_1_p2[27], ~mipsprogramrom_1_p2[28], mipsprogramrom_1_p2[29], ~mipsprogramrom_1_p2[30], mipsprogramrom_1_p2[31]);  // AND_Gate
  and and_5 (and_5_out, mipsprogramrom_1_p2[26], mipsprogramrom_1_p2[27], ~mipsprogramrom_1_p2[28], ~mipsprogramrom_1_p2[29], ~mipsprogramrom_1_p2[30], mipsprogramrom_1_p2[31]);  // AND_Gate
  or or_1 (ALU_OP[1], and_3_out, and_2_out, ALU_OP[3]);
  assign bit_extender_1_out = {{16{1'b0}}, {mipsprogramrom_1_p2[15:6], FUNCT}};  // Bit_Extender bit_extender_1
  or or_2 (REG_DEST, and_3_out, and_4_out, and_5_out);
  or or_3 (ALU_SRC, and_3_out, and_4_out, and_5_out);
  or or_4 (REG_W, and_3_out, and_4_out, and_2_out, and_3_out, ALU_OP[3]);
  and and_6 (STORE, and_4_out, ~and_5_out);  // AND_Gate
  and and_7 (LOAD, ~and_4_out, and_5_out);  // AND_Gate
  and and_8 (MEM_TO_REG, ~and_3_out, ~and_4_out, and_5_out);  // AND_Gate
  // RegisterFile registerfile_1: pin names not known; wires that end beside it: registerfile_1_p1, CLOCK, REG_W, multiplexer_1_out, mipsprogramrom_1_p2_2, mipsprogramrom_1_p2[20:16], registerfile_1_p7, registerfile_1_p8
  Multiplexer #(.width(32)) multiplexer_2 (
    .in0(registerfile_1_p8), .in1(bit_extender_1_out), .out(multiplexer_2_out), .sel(ALU_SRC));  // open: en
  // Mips_ALU mips_alu_1: pin names not known; wires that end beside it: registerfile_1_p7, multiplexer_2_out, {{2{ALU_OP[3]}}, ALU_OP[1], 1'b0}, mips_alu_1_p4
  // MIPS_RAM mips_ram_1: pin names not known; wires that end beside it: mips_alu_1_p4[19:0], STORE, CLOCK, LOAD, mips_ram_1_p5
  Multiplexer #(.width(32)) multiplexer_3 (
    .in0(mips_alu_1_p4), .in1(mips_ram_1_p5), .out(registerfile_1_p1), .sel(MEM_TO_REG));  // open: en

  // Other names for the same wires on the sheet: ALU_OP[2] = ALU_OP[3]

  // Notes on the sheet:
  //   OP
  //   NOR
  //   Funct S.A
  //   R
  //   I
  //   Imediato do tipo I
  //   ADDIU
  //   STORE
  //   LOAD
  //   ADDU
  //   Endereco a ser gravado
  //   Endereco do registrador lido por A
  //   Endereco do registrador lido por B
  //   Habilita a gravação
  //   Converte o imediato para 32 Bits
  //   R
  //   I
  //   Endereco base
  //   Offset do imediato
  //   Operação a ser realizada
  //   Dado a ser guardado
  //   Liga somente para o load
endmodule
